// Logisim project Project-1.circ as structural Verilog: 4 circuits, main circuit main
module main (
);

  wire clock_1_out, dec_counter_1__0, dec_counter_1__1, dec_counter_1__2, dec_counter_1__3,
       n8421bcd_dec_driver_1_a, n8421bcd_dec_driver_1_b, n8421bcd_dec_driver_1_c, n8421bcd_dec_driver_1_d,
       n8421bcd_dec_driver_1_e, n8421bcd_dec_driver_1_f, n8421bcd_dec_driver_1_out_11;

  Clock clock_1 (.out(clock_1_out));
  dec_counter dec_counter_1 (
    .Clock(clock_1_out), ._0(dec_counter_1__0), ._1(dec_counter_1__1), ._2(dec_counter_1__2),
    ._3(dec_counter_1__3));  // open: IS_NINE
  _8421bcd_dec_driver u_8421bcd_dec_driver_1 (
    .w(dec_counter_1__3), .x(dec_counter_1__2), .y(dec_counter_1__1), .z(dec_counter_1__0),
    .a(n8421bcd_dec_driver_1_a), .b(n8421bcd_dec_driver_1_b), .c(n8421bcd_dec_driver_1_c),
    .d(n8421bcd_dec_driver_1_d), .e(n8421bcd_dec_driver_1_e), .f(n8421bcd_dec_driver_1_f),
    .out_11(n8421bcd_dec_driver_1_out_11));
  _7_Segment_Display u_7_segment_display_1 (
    .g(n8421bcd_dec_driver_1_out_11), .f(n8421bcd_dec_driver_1_f), .a(n8421bcd_dec_driver_1_a),
    .b(n8421bcd_dec_driver_1_b), .e(n8421bcd_dec_driver_1_e), .d(n8421bcd_dec_driver_1_d),
    .c(n8421bcd_dec_driver_1_c));  // open: dp
endmodule

module bonus (
);

  wire clock_1_out, dec_counter_1__0, dec_counter_1__1, dec_counter_1__2, dec_counter_1__3, dec_counter_2__0,
       dec_counter_2__1, dec_counter_2__2, dec_counter_2__3, dec_counter_2_is_nine, n8421bcd_dec_driver_1_a,
       n8421bcd_dec_driver_1_b, n8421bcd_dec_driver_1_c, n8421bcd_dec_driver_1_d, n8421bcd_dec_driver_1_e,
       n8421bcd_dec_driver_1_f, n8421bcd_dec_driver_1_out_11, n8421bcd_dec_driver_2_a,
       n8421bcd_dec_driver_2_b, n8421bcd_dec_driver_2_c, n8421bcd_dec_driver_2_d, n8421bcd_dec_driver_2_e,
       n8421bcd_dec_driver_2_f, n8421bcd_dec_driver_2_out_11;

  dec_counter dec_counter_1 (
    .Clock(dec_counter_2_is_nine), ._0(dec_counter_1__0), ._1(dec_counter_1__1), ._2(dec_counter_1__2),
    ._3(dec_counter_1__3));  // open: IS_NINE
  _8421bcd_dec_driver u_8421bcd_dec_driver_1 (
    .w(dec_counter_1__3), .x(dec_counter_1__2), .y(dec_counter_1__1), .z(dec_counter_1__0),
    .a(n8421bcd_dec_driver_1_a), .b(n8421bcd_dec_driver_1_b), .c(n8421bcd_dec_driver_1_c),
    .d(n8421bcd_dec_driver_1_d), .e(n8421bcd_dec_driver_1_e), .f(n8421bcd_dec_driver_1_f),
    .out_11(n8421bcd_dec_driver_1_out_11));
  _7_Segment_Display u_7_segment_display_1 (
    .g(n8421bcd_dec_driver_2_out_11), .f(n8421bcd_dec_driver_2_f), .a(n8421bcd_dec_driver_2_a),
    .b(n8421bcd_dec_driver_2_b), .e(n8421bcd_dec_driver_2_e), .d(n8421bcd_dec_driver_2_d),
    .c(n8421bcd_dec_driver_2_c));  // open: dp
  _7_Segment_Display u_7_segment_display_2 (
    .g(n8421bcd_dec_driver_1_out_11), .f(n8421bcd_dec_driver_1_f), .a(n8421bcd_dec_driver_1_a),
    .b(n8421bcd_dec_driver_1_b), .e(n8421bcd_dec_driver_1_e), .d(n8421bcd_dec_driver_1_d),
    .c(n8421bcd_dec_driver_1_c));  // open: dp
  _8421bcd_dec_driver u_8421bcd_dec_driver_2 (
    .w(dec_counter_2__3), .x(dec_counter_2__2), .y(dec_counter_2__1), .z(dec_counter_2__0),
    .a(n8421bcd_dec_driver_2_a), .b(n8421bcd_dec_driver_2_b), .c(n8421bcd_dec_driver_2_c),
    .d(n8421bcd_dec_driver_2_d), .e(n8421bcd_dec_driver_2_e), .f(n8421bcd_dec_driver_2_f),
    .out_11(n8421bcd_dec_driver_2_out_11));
  dec_counter dec_counter_2 (
    .Clock(clock_1_out), .IS_NINE(dec_counter_2_is_nine), ._0(dec_counter_2__0), ._1(dec_counter_2__1),
    ._2(dec_counter_2__2), ._3(dec_counter_2__3));
  Clock clock_1 (.out(clock_1_out));
endmodule

module _8421bcd_dec_driver (
  input  w,
  input  x,
  input  y,
  input  z,
  output a,
  output b,
  output c,
  output d,
  output e,
  output f,
  output out_11
);

  wire not_1_out, not_2_out, not_3_out, not_4_out, x_prime_y_out, x_prime_z_prime_out, xy_prime_out,
       xy_prime_z_out, xz_out, xz_prime_out, y_prime_z_prime_out, yz_out, yz_prime_out;

  not not_1 (not_1_out, w);
  not not_2 (not_2_out, x);
  not not_3 (not_3_out, y);
  not not_4 (not_4_out, z);
  and xz (xz_out, x, z);
  and x_prime_z_prime (x_prime_z_prime_out, not_2_out, not_4_out);
  and yz (yz_out, y, z);
  and y_prime_z_prime (y_prime_z_prime_out, not_3_out, not_4_out);
  and yz_prime (yz_prime_out, y, not_4_out);
  and x_prime_y (x_prime_y_out, not_2_out, y);
  and xy_prime (xy_prime_out, x, not_3_out);
  and xz_prime (xz_prime_out, x, not_4_out);
  and xy_prime_z (xy_prime_z_out, z, xy_prime_out);
  or or_1 (a, xz_out, x_prime_z_prime_out, w, y);
  or or_2 (b, yz_out, y_prime_z_prime_out, not_2_out);
  or or_3 (c, x, not_3_out, z);
  or or_4 (d, w, x_prime_z_prime_out, yz_prime_out, x_prime_y_out, xy_prime_z_out);
  or or_5 (e, yz_prime_out, x_prime_z_prime_out);
  or or_6 (f, xy_prime_out, xz_prime_out, y_prime_z_prime_out, w);
  or or_7 (out_11, yz_prime_out, xy_prime_out, w, x_prime_y_out);
endmodule

module dec_counter (
  input  Clock,
  output _0,
  output _1,
  output _2,
  output _3,
  output IS_NINE
);

  wire and_2_out, and_3_out, and_4_out, and_5_out, and_6_out, and_7_out, and_8_out, D1_qn, D2_qn, D3_qn,
       D4_qn, or_1_out, or_2_out, or_3_out;

  and and_1 (IS_NINE, _3, D2_qn, D3_qn, _0);
  and and_2 (and_2_out, _3, D4_qn);
  and and_3 (and_3_out, _2, _1, _0);
  and and_4 (and_4_out, _2, D3_qn);
  and and_5 (and_5_out, _2, D4_qn);
  and and_6 (and_6_out, D2_qn, _1, _0);
  and and_7 (and_7_out, _1, D4_qn);
  and and_8 (and_8_out, D1_qn, D3_qn, _0);
  or or_1 (or_1_out, and_2_out, and_3_out);
  or or_2 (or_2_out, and_4_out, and_5_out, and_6_out);
  or or_3 (or_3_out, and_7_out, and_8_out);
  D_Flip_Flop #(.trigger("falling")) D1 (.clk(Clock), .D(or_1_out), .Q(_3), .Qn(D1_qn));  // open: preset, en, reset
  D_Flip_Flop #(.trigger("falling")) D2 (.clk(Clock), .D(or_2_out), .Q(_2), .Qn(D2_qn));  // open: preset, en, reset
  D_Flip_Flop #(.trigger("falling")) D3 (.clk(Clock), .D(or_3_out), .Q(_1), .Qn(D3_qn));  // open: preset, en, reset
  D_Flip_Flop #(.trigger("falling")) D4 (.clk(Clock), .D(D4_qn), .Q(_0), .Qn(D4_qn));  // open: preset, en, reset
endmodule
