// Logisim project project2.circ as structural Verilog: 5 circuits, main circuit main
module main (
  input  in_1,
  input  in_2,
  input  in_3,
  input  in_4,
  input  in_5,
  input  in_6,
  input  in_7,
  input  in_8,
  input  in_9
);

  wire b2d_1_a_2, b2d_1_b_2, b2d_1_c_2, b2d_1_d_2, b2d_1_e, b2d_1_f, b2d_1_g, b2d_2_a_2, b2d_2_b_2,
       b2d_2_c_2, b2d_2_d_2, b2d_2_e, b2d_2_f, b2d_2_g, b2d_3_a_2, b2d_3_b_2, b2d_3_c_2, b2d_3_d_2, b2d_3_e,
       b2d_3_f, b2d_3_g, b2d_4_a_2, b2d_4_b_2, b2d_4_c_2, b2d_4_d_2, b2d_4_e, b2d_4_f, b2d_4_g,
       n4_bit_full_adder_1_cout, n4_bit_full_adder_1_s1, n4_bit_full_adder_1_s2, n4_bit_full_adder_1_s3,
       n4_bit_full_adder_1_s4, n4_bit_full_adder_2_cout, n4_bit_full_adder_2_s1, n4_bit_full_adder_2_s2,
       n4_bit_full_adder_2_s3, n4_bit_full_adder_2_s4, subadder_1_b1out, subadder_1_b2out, subadder_1_b3out,
       subadder_1_b4out, subadder_2_b1out, subadder_2_b2out, subadder_2_b3out, subadder_2_b4out;

  b2d b2d_1 (
    .D(in_1), .C(in_2), .B(in_3), .A(in_4), .a_2(b2d_1_a_2), .b_2(b2d_1_b_2), .c_2(b2d_1_c_2),
    .d_2(b2d_1_d_2), .e(b2d_1_e), .f(b2d_1_f), .g(b2d_1_g));
  _7_Segment_Display u_7_segment_display_1 (
    .g(b2d_1_g), .f(b2d_1_f), .a(b2d_1_a_2), .b(b2d_1_b_2), .e(b2d_1_e), .d(b2d_1_d_2), .c(b2d_1_c_2));  // open: dp
  b2d b2d_2 (
    .D(in_5), .C(in_6), .B(in_7), .A(in_8), .a_2(b2d_2_a_2), .b_2(b2d_2_b_2), .c_2(b2d_2_c_2),
    .d_2(b2d_2_d_2), .e(b2d_2_e), .f(b2d_2_f), .g(b2d_2_g));
  _7_Segment_Display u_7_segment_display_2 (
    .g(b2d_2_g), .f(b2d_2_f), .a(b2d_2_a_2), .b(b2d_2_b_2), .e(b2d_2_e), .d(b2d_2_d_2), .c(b2d_2_c_2));  // open: dp
  subadder subadder_1 (
    .ctrl(in_9), .B1in(in_4), .B2in(in_3), .B3in(in_2), .B4in(in_1), .B1out(subadder_1_b1out),
    .B2out(subadder_1_b2out), .B3out(subadder_1_b3out), .B4out(subadder_1_b4out));
  subadder subadder_2 (
    .ctrl(in_1), .B1in(in_9), .B2in(in_9), .B3in(in_9), .B4in(in_1), .B1out(subadder_2_b1out),
    .B2out(subadder_2_b2out), .B3out(subadder_2_b3out), .B4out(subadder_2_b4out));
  _4_bit_full_adder u_4_bit_full_adder_1 (
    .a4(subadder_1_b4out), .b4(subadder_1_b3out), .a3(subadder_1_b2out), .b3(subadder_1_b1out), .a2(in_9),
    .b2(in_5), .a1(in_6), .b1(in_7), .in_9(in_8), .Cout(n4_bit_full_adder_1_cout),
    .s4(n4_bit_full_adder_1_s4), .s3(n4_bit_full_adder_1_s3), .s2(n4_bit_full_adder_1_s2),
    .s1(n4_bit_full_adder_1_s1));
  _4_bit_full_adder u_4_bit_full_adder_2 (
    .a4(subadder_2_b4out), .b4(subadder_2_b3out), .a3(subadder_2_b2out), .b3(subadder_2_b1out), .a2(in_1),
    .b2(in_1), .a1(in_9), .b1(in_9), .in_9(in_9), .Cout(n4_bit_full_adder_2_cout),
    .s4(n4_bit_full_adder_2_s4), .s3(n4_bit_full_adder_2_s3), .s2(n4_bit_full_adder_2_s2),
    .s1(n4_bit_full_adder_2_s1));
  b2d b2d_3 (
    .D(n4_bit_full_adder_2_cout), .C(n4_bit_full_adder_2_s1), .B(n4_bit_full_adder_2_s1),
    .A(n4_bit_full_adder_2_s1), .a_2(b2d_3_a_2), .b_2(b2d_3_b_2), .c_2(b2d_3_c_2), .d_2(b2d_3_d_2),
    .e(b2d_3_e), .f(b2d_3_f), .g(b2d_3_g));
  _7_Segment_Display u_7_segment_display_3 (
    .g(b2d_3_g), .f(b2d_3_f), .a(b2d_3_a_2), .b(b2d_3_b_2), .e(b2d_3_e), .d(b2d_3_d_2), .c(b2d_3_c_2));  // open: dp
  b2d b2d_4 (
    .D(n4_bit_full_adder_1_s4), .C(n4_bit_full_adder_1_s3), .B(n4_bit_full_adder_1_s2),
    .A(n4_bit_full_adder_1_s1), .a_2(b2d_4_a_2), .b_2(b2d_4_b_2), .c_2(b2d_4_c_2), .d_2(b2d_4_d_2),
    .e(b2d_4_e), .f(b2d_4_f), .g(b2d_4_g));
  _7_Segment_Display u_7_segment_display_4 (
    .g(b2d_4_g), .f(b2d_4_f), .a(b2d_4_a_2), .b(b2d_4_b_2), .e(b2d_4_e), .d(b2d_4_d_2), .c(b2d_4_c_2));  // open: dp
endmodule

module b2d (
  input  D,
  input  C,
  input  B,
  input  A,
  output a_2,
  output b_2,
  output c_2,
  output d_2,
  output e,
  output f,
  output g
);

  wire and_1_out, and_2_out, and_3_out, and_4_out, and_5_out, and_6_out, and_7_out, and_8_out, and_9_out,
       and_10_out, and_11_out, and_12_out, and_13_out, and_14_out, and_15_out, and_16_out, not_1_out,
       not_2_out, not_3_out, not_4_out, not_5_out, not_6_out, not_7_out, not_8_out, not_9_out, not_10_out,
       not_11_out, not_12_out, not_13_out, not_14_out, not_15_out, not_16_out, not_17_out, not_18_out,
       not_19_out, not_20_out, not_21_out;

  not not_1 (not_1_out, C);
  and and_1 (and_1_out, not_1_out, not_2_out);
  not not_2 (not_2_out, A);
  and and_2 (and_2_out, C, A);
  not not_3 (not_3_out, C);
  not not_4 (not_4_out, B);
  and and_3 (and_3_out, not_4_out, not_5_out);
  not not_5 (not_5_out, A);
  and and_4 (and_4_out, B, A);
  not not_6 (not_6_out, B);
  or or_1 (c_2, not_6_out, A, C);
  not not_7 (not_7_out, C);
  and and_5 (and_5_out, not_7_out, not_8_out);
  not not_8 (not_8_out, A);
  not not_9 (not_9_out, C);
  and and_6 (and_6_out, not_9_out, B);
  and and_7 (and_7_out, B, not_10_out);
  not not_10 (not_10_out, A);
  and and_8 (and_8_out, C, not_11_out, A);
  not not_11 (not_11_out, B);
  not not_12 (not_12_out, C);
  and and_9 (and_9_out, not_12_out, not_13_out);
  not not_13 (not_13_out, A);
  and and_10 (and_10_out, B, not_14_out);
  not not_14 (not_14_out, A);
  not not_15 (not_15_out, B);
  and and_11 (and_11_out, not_15_out, not_16_out);
  not not_16 (not_16_out, A);
  and and_12 (and_12_out, C, not_17_out);
  not not_17 (not_17_out, B);
  and and_13 (and_13_out, C, not_18_out);
  not not_18 (not_18_out, A);
  not not_19 (not_19_out, C);
  and and_14 (and_14_out, not_19_out, B);
  and and_15 (and_15_out, C, not_20_out);
  not not_20 (not_20_out, B);
  and and_16 (and_16_out, C, not_21_out);
  not not_21 (not_21_out, A);
  or or_2 (a_2, and_1_out, B, and_2_out, D);
  or or_3 (b_2, not_3_out, and_3_out, and_4_out);
  or or_4 (d_2, and_5_out, and_6_out, and_7_out, and_8_out, D);
  or or_5 (e, and_9_out, and_10_out);
  or or_6 (f, and_11_out, and_12_out, and_13_out, D);
  or or_7 (g, and_14_out, and_15_out, and_16_out, D);
endmodule

module full_adder (
  input  A,
  input  B,
  input  Cin,
  output S,
  output Cout
);

  wire and_1_out, and_2_out, xor_1_out;

  xor xor_1 (xor_1_out, A, B);
  buf and_1 (and_1_out, Cin);  // AND_Gate
  and and_2 (and_2_out, B, Cin);
  xor xor_2 (S, xor_1_out, Cin);
  xor xor_3 (Cout, and_1_out, and_2_out);
endmodule

module _4_bit_full_adder (
  input  a4,
  input  b4,
  input  a3,
  input  b3,
  input  a2,
  input  b2,
  input  a1,
  input  b1,
  input  in_9,
  output Cout,
  output s4,
  output s3,
  output s2,
  output s1
);

  wire full_adder_2_cout, full_adder_3_cout, full_adder_4_cout;

  full_adder full_adder_1 (.A(full_adder_2_cout), .B(b4), .Cin(a4), .S(s4), .Cout(Cout));
  full_adder full_adder_2 (.A(full_adder_3_cout), .B(b3), .Cin(a3), .S(s3), .Cout(full_adder_2_cout));
  full_adder full_adder_3 (.A(full_adder_4_cout), .B(b2), .Cin(a2), .S(s2), .Cout(full_adder_3_cout));
  full_adder full_adder_4 (.A(in_9), .B(a1), .Cin(a1), .S(s1), .Cout(full_adder_4_cout));

  assign b1 = a1;
endmodule

module subadder (
  input  ctrl,
  input  B1in,
  input  B2in,
  input  B3in,
  input  B4in,
  output B1out,
  output B2out,
  output B3out,
  output B4out
);

  wire and_1_out, and_2_out, and_3_out, and_4_out, and_5_out, and_6_out, and_7_out, and_8_out, not_1_out,
       not_2_out, not_3_out, not_4_out, not_5_out;

  not not_1 (not_1_out, ctrl);
  not not_2 (not_2_out, B1in);
  not not_3 (not_3_out, B2in);
  not not_4 (not_4_out, B3in);
  not not_5 (not_5_out, B4in);
  and and_1 (and_1_out, not_1_out, B1in);
  and and_2 (and_2_out, ctrl, not_2_out);
  and and_3 (and_3_out, not_1_out, B2in);
  and and_4 (and_4_out, ctrl, not_3_out);
  and and_5 (and_5_out, not_1_out, B3in);
  and and_6 (and_6_out, ctrl, not_4_out);
  and and_7 (and_7_out, not_1_out, B4in);
  and and_8 (and_8_out, ctrl, not_5_out);
  or or_1 (B1out, and_1_out, and_2_out);
  or or_2 (B2out, and_3_out, and_4_out);
  or or_3 (B3out, and_5_out, and_6_out);
  or or_4 (B4out, and_7_out, and_8_out);
endmodule
